# Fritzing sketch simple (saved by Fritzing 0.9.3b)

parts:
  Part1 = Arduino Uno (Rev3)
  Part2 = Arduino Nano (Rev3.0)
  microSD1 = MicroSD Card Module

nets:
  N1: Part1.D0/RX, Part2.D1/TX
  N2: Part1.D1/TX, Part2.D0/RX
  N3: Part2.D10, microSD1.MISO
  N4: Part2.D11/MOSI, microSD1.MOSI
  N5: Part2.D12/MISO, microSD1.SCK
  GND: Part2.GND, microSD1.GND
  5V: Part2.5V, microSD1.VCC
  N6: Part2.D13/SCK, microSD1.CS
